# Fritzing sketch ioioMotorControl (saved by Fritzing 0.7.12b)
breadboards: 1

parts:
  Part1 = TB6612FNG Breakout v11
  Part2 = IOIO for Android
  M1 = DC Motor
  M2 = DC Motor
  BATT1 = LiPoly Battery (1300mAh)

nets:
  N1: Part1.B01, M2.pin_1
  N2: Part1.B02, M2.pin_2
  N3: Part1.A02, M1.pin_1
  N4: Part1.A01, M1.pin_2
  GND: Part1.GND, Part2.GND, BATT1.negative
  VCC: Part1.VCC, Part2.3.3V
  N5: Part1.VM, BATT1.positive
  N6: Part1.PWMA, Part2.PIN30
  N7: Part1.AIN2, Part2.PIN31
  N8: Part1.AIN1, Part2.PIN32
  N9: Part1.STBY, Part2.PIN42
  N10: Part1.BIN1, Part2.PIN43
  N11: Part1.BIN2, Part2.PIN44
  N12: Part1.PWMB, Part2.PIN45

custom parts:
  LiPoly Battery (1300mAh): Lithium Ion Polymer Battery (1300mAh)
